# Fritzing sketch Frizting_Projet_V2 (saved by Fritzing 0.9.3b)
breadboards: 2

parts:
  Arduino = Arduino Uno (Rev3)
  R1 = Resistor [tolerance=±5% resistance=10k package=THT]
  R2 = Resistor [tolerance=±5% resistance=220 package=THT]
  C2 = Ceramic Capacitor [capacitance=10nF package="100 mil [THT, multilayer]"]
  L1 = Inductor [package="0603 [SMD]"]
  C3 = Ceramic Capacitor [capacitance=0.1nF package="100 mil [THT, multilayer]"]
  R3 = Resistor [tolerance=±5% resistance=1M package=THT]
  D1 = Rectifier Diode [part_number=1N4001 package="Melf DO-213 AB [SMD]"]
  U1 = TOUCH [package=touch1]
  LED1 = LED - 3mm [color="Red (633nm)" package="3 mm [THT]"]
  R4 = Resistor [tolerance=±5% resistance=220 package="2512 [SMD]"]
  R5 = Resistor [tolerance=±5% resistance=220 package="0805 [SMD]"]
  Piezo_Speaker = Piezo Speaker

nets (from the schematic view):
  N1: Arduino.D9_PWM, R1.Pin_1
  N2: Arduino.GND, R2.Pin_1, C3.1, R3.Pin_0
  N3: Arduino.D3_PWM, R5.Pin_0
  N4: R1.Pin_0, R2.Pin_0, L1.pin_1
  N5: C2.0, L1.pin_0
  N6: C2.1, C3.0, D1.anode, U1.T1, U1.T2
  N7: LED1.cathode, Piezo_Speaker.pin2
  N8: LED1.anode, R4.Pin_1
  N9: R5.Pin_1, Piezo_Speaker.pin1

notes:
  = Patate
